# Fritzing sketch rfid_oled_nodemcu (saved by Fritzing 0.9.10b)

parts:
  Mod1 = Amica NodeMCU DEVKIT 1.0
  Parça1 = RFID-RC522-v2
  OLED_I2C1 = OLED 128x64 I2C Monochrome Display

nets:
  3.3V: Mod1.pin1, Mod1.pin_10, Mod1.pin_26, Parça1.3.3V, OLED_I2C1.VDD
  N1: Mod1.pin6, Parça1.MOSI
  N2: Mod1.pin7, Parça1.MISO
  N3: Mod1.pin8, Parça1.SCK
  GND: Mod1.pin_9, Mod1.pin_25, Mod1.pin_29, Parça1.GND, OLED_I2C1.GND
  N4: Mod1.pin_12, Parça1.SDA
  N5: Mod1.pin_13, OLED_I2C1.SDA
  N6: Mod1.pin_14, OLED_I2C1.SCK
  N7: Mod1.pin_15, Parça1.RST

custom parts:
  RFID-RC522-v2: A simple China made RFID-RC522 Reader; do check the pin labels, as this is a MFRC522 based clone.
